# Fritzing sketch robot-V1-1 (saved by Fritzing 0.9.3b)
breadboards: 1

parts:
  J1 = Infrared Proximity Sensor
  hc-sr1 = hc-sr04
  hc-sr2 = hc-sr04
  IC1 = L293D [package=THT]
  M1 = DC Motor
  M2 = DC Motor
  Composant1 = Arduino Nano (Rev3.0)
  VCC1 = 4 x AAA Battery Mount

nets:
  N1: J1.Vout, Composant1.A7
  GND: J1.GND, hc-sr1.GND, hc-sr2.GND, Composant1.GND, VCC1.-
  VCC: J1.Vcc, hc-sr1.VCC, hc-sr2.VCC, IC1.Enable_1, IC1.+Vmotor, IC1.Enable_2, IC1.+V, VCC1.+
  N2: hc-sr1.Trig, Composant1.D4
  N3: hc-sr1.Echo, Composant1.D5
  N4: hc-sr2.Trig, Composant1.D2
  N5: hc-sr2.Echo, Composant1.D3
  N6: IC1.In_1, Composant1.D10
  N7: IC1.Out_1_(_Controlled_by_Enable_1_), M2.pin_1
  N8: IC1.Out_2_(_Controlled_by_Enable_1_), M2.pin_2
  N9: IC1.In_2, Composant1.D9
  N10: IC1.In_3, Composant1.D7
  N11: IC1.Out_3_(_Controlled_by_Enable_2_), M1.pin_2
  N12: IC1.Out_4_(_Controlled_by_Enable_2_), M1.pin_1
  N13: IC1.In_4, Composant1.D8

notes:
  Motor
  power 5v
  ultrasound sensor
  distance sensor
